// Logisim project 2nd_1 bit ALU.circ as structural Verilog: 1 circuit, main circuit main
module main (
  input  CLK,
  input  T5,
  input  D0,
  input  D1,
  input  LOAD,
  input  D2,
  input  D6,
  input  T3,
  input  D7,
  input  I,
  input  IR_5,
  input  IR_6,
  input  IR_7,
  input  IR_9,
  input  IR_11,
  input  INPR___i__th_BIT,
  input  AC_i_1,
  input  AC_i_1_2,
  input  c_in__add,
  input  DR_i,
  input  c_in__sub,
  input  C_IN_INC,
  input  AC__i,
  output AC__i_2,
  output c_out,
  output c_out_sub,
  output c_out_add
);

  wire ADD_out, adder_1_out, adder_2_out, and_2_out, and_3_out, AND_out, COM_out, DR_out, INC_out, INPR_out,
       main_1_add, main_1_and, main_1_clr, main_1_com, main_1_dr, main_1_inc, main_1_inpr, main_1_shl,
       main_1_shr, main_1_sub, not_1_out, not_2_out, or_1_out, SHL_out, SHR_out, SUB_out, subtractor_1_out;

  AC_LOAD_MAIN_main main_1 (
    .t5(T5), .D0(D0), .D1(D1), .D2(D2), .D6(D6), .T3(T3), .D7(D7), .I(I), .IR_5(IR_6), .IR_6(IR_5),
    .IR_7(IR_7), .IR_9(IR_9), .ir_11(IR_11), .AND(main_1_and), .ADD(main_1_add), .DR(main_1_dr),
    .SUB(main_1_sub), .clr(main_1_clr), .INC(main_1_inc), .SHL(main_1_shl), .SHR(main_1_shr),
    .COM(main_1_com), .INPR(main_1_inpr));
  not not_1 (not_1_out, AC__i);
  Adder #(.width(1)) adder_1 (.a(DR_i), .b(AC__i), .out(adder_1_out), .cin(c_in__add), .cout(c_out_add));
  and AND (AND_out, main_1_and, DR_i, AC__i);
  and ADD (ADD_out, main_1_add, adder_1_out);
  and DR (DR_out, main_1_dr, DR_i);
  and INC (INC_out, main_1_inc, adder_2_out);
  and SUB (SUB_out, main_1_sub, subtractor_1_out);
  and SHL (SHL_out, main_1_shl, AC_i_1);
  and SHR (SHR_out, main_1_shr, AC_i_1_2);
  and COM (COM_out, main_1_com, not_1_out);
  and INPR (INPR_out, main_1_inpr, INPR___i__th_BIT);
  Subtractor #(.width(1)) subtractor_1 (.a(AC__i), .b(DR_i), .out(subtractor_1_out), .bin(c_in__sub), .bout(c_out_sub));
  or or_1 (or_1_out, AND_out, ADD_out, DR_out, SUB_out, INC_out, SHL_out, SHR_out, COM_out, INPR_out);
  Adder #(.width(1)) adder_2 (.a(1'b1), .b(AC__i), .out(adder_2_out), .cin(C_IN_INC), .cout(c_out));
  not not_2 (not_2_out, or_1_out);
  Clock clock_1 ();  // open: out
  and and_2 (and_2_out, LOAD, or_1_out);
  and and_3 (and_3_out, not_2_out, LOAD);
  J_K_Flip_Flop j_k_ff_1 (
    .J(and_2_out), .clk(CLK), .K(and_3_out), .Q(AC__i_2), .en(LOAD), .reset(main_1_clr));  // open: Qn, preset
endmodule
