// Logisim project 8 BIT Arithmatic unit.circ as structural Verilog: 3 circuits, main circuit main
module main (
  input  Cin,
  input  B0,
  input  A0,
  input  in_4,
  input  in_5,
  input  B1,
  input  A1,
  input  in_8,
  input  in_9,
  input  B2,
  input  A2,
  input  in_12,
  input  in_13,
  input  B3,
  input  A3,
  input  in_16,
  input  in_17,
  input  B4,
  input  A0_2,
  input  in_20,
  input  in_21,
  input  B5,
  input  A1_2,
  input  in_24,
  input  in_25,
  input  B6,
  input  A2_2,
  input  in_28,
  input  in_29,
  input  B7,
  input  A3_2,
  input  in_32,
  input  in_33,
  input  [1:0] in_34,
  output D0,
  output D1,
  output D2,
  output D3,
  output D4,
  output D5,
  output D6,
  output D7
);

  wire adder_1_cout, adder_2_cout, adder_3_cout, adder_4_cout, adder_5_cout, adder_6_cout, adder_7_cout,
       multiplexer_1_out, multiplexer_2_out, multiplexer_3_out, multiplexer_4_out, multiplexer_5_out,
       multiplexer_6_out, multiplexer_7_out, multiplexer_8_out, not_1_out, not_2_out, not_3_out, not_4_out,
       not_5_out, not_6_out, not_7_out, not_8_out;

  not not_1 (not_1_out, B0);
  not not_2 (not_2_out, B1);
  not not_3 (not_3_out, B2);
  not not_4 (not_4_out, B3);
  not not_5 (not_5_out, B4);
  not not_6 (not_6_out, B5);
  not not_7 (not_7_out, B6);
  not not_8 (not_8_out, B7);
  Multiplexer #(.select(2), .disabled(0)) multiplexer_1 (
    .in0(B0), .in1(not_1_out), .in2(in_4), .in3(in_5), .out(multiplexer_1_out), .sel(in_34));  // open: en
  Multiplexer #(.select(2), .disabled(0)) multiplexer_2 (
    .in0(B1), .in1(not_2_out), .in2(in_8), .in3(in_9), .out(multiplexer_2_out), .sel(in_34));  // open: en
  Multiplexer #(.select(2), .disabled(0)) multiplexer_3 (
    .in0(B2), .in1(not_3_out), .in2(in_12), .in3(in_13), .out(multiplexer_3_out), .sel(in_34));  // open: en
  Multiplexer #(.select(2), .disabled(0)) multiplexer_4 (
    .in0(B3), .in1(not_4_out), .in2(in_16), .in3(in_17), .out(multiplexer_4_out), .sel(in_34));  // open: en
  Multiplexer #(.select(2), .disabled(0)) multiplexer_5 (
    .in0(B4), .in1(not_5_out), .in2(in_20), .in3(in_21), .out(multiplexer_5_out), .sel(in_34));  // open: en
  Multiplexer #(.select(2), .disabled(0)) multiplexer_6 (
    .in0(B5), .in1(not_6_out), .in2(in_24), .in3(in_25), .out(multiplexer_6_out), .sel(in_34));  // open: en
  Multiplexer #(.select(2), .disabled(0)) multiplexer_7 (
    .in0(B6), .in1(not_7_out), .in2(in_28), .in3(in_29), .out(multiplexer_7_out), .sel(in_34));  // open: en
  Multiplexer #(.select(2), .disabled(0)) multiplexer_8 (
    .in0(B7), .in1(not_8_out), .in2(in_32), .in3(in_33), .out(multiplexer_8_out), .sel(in_34));  // open: en
  Adder #(.width(1)) adder_1 (.a(A0), .b(multiplexer_1_out), .out(D0), .cin(Cin), .cout(adder_1_cout));
  Adder #(.width(1)) adder_2 (.a(A1), .b(multiplexer_2_out), .out(D1), .cin(adder_1_cout), .cout(adder_2_cout));
  Adder #(.width(1)) adder_3 (.a(A2), .b(multiplexer_3_out), .out(D2), .cin(adder_2_cout), .cout(adder_3_cout));
  Adder #(.width(1)) adder_4 (.a(A3), .b(multiplexer_4_out), .out(D3), .cin(adder_3_cout), .cout(adder_4_cout));
  Adder #(.width(1)) adder_5 (.a(A0_2), .b(multiplexer_5_out), .out(D4), .cin(adder_4_cout), .cout(adder_5_cout));
  Adder #(.width(1)) adder_6 (.a(A1_2), .b(multiplexer_6_out), .out(D5), .cin(adder_5_cout), .cout(adder_6_cout));
  Adder #(.width(1)) adder_7 (.a(A2_2), .b(multiplexer_7_out), .out(D6), .cin(adder_6_cout), .cout(adder_7_cout));
  Adder #(.width(1)) adder_8 (.a(A3_2), .b(multiplexer_8_out), .out(D7), .cin(adder_7_cout));  // open: cout
endmodule

module ARITHMATIC_UNIT (
  input  Cin,
  input  B0,
  input  A0,
  input  in_4,
  input  in_5,
  input  B1,
  input  A1,
  input  in_8,
  input  in_9,
  input  B2,
  input  A2,
  input  in_12,
  input  in_13,
  input  B3,
  input  A3,
  input  in_16,
  input  in_17,
  input  B4,
  input  A0_2,
  input  in_20,
  input  in_21,
  input  B5,
  input  A1_2,
  input  in_24,
  input  in_25,
  input  B6,
  input  A2_2,
  input  in_28,
  input  in_29,
  input  B7,
  input  A3_2,
  input  in_32,
  input  in_33,
  input  [1:0] in_34,
  output D0,
  output D1,
  output D2,
  output D3,
  output D4,
  output D5,
  output D6,
  output D7
);

  wire adder_1_cout, adder_2_cout, adder_3_cout, adder_4_cout, adder_5_cout, adder_6_cout, adder_7_cout,
       multiplexer_1_out, multiplexer_2_out, multiplexer_3_out, multiplexer_4_out, multiplexer_5_out,
       multiplexer_6_out, multiplexer_7_out, multiplexer_8_out, not_1_out, not_2_out, not_3_out, not_4_out,
       not_5_out, not_6_out, not_7_out, not_8_out;

  not not_1 (not_1_out, B0);
  not not_2 (not_2_out, B1);
  not not_3 (not_3_out, B2);
  not not_4 (not_4_out, B3);
  not not_5 (not_5_out, B4);
  not not_6 (not_6_out, B5);
  not not_7 (not_7_out, B6);
  not not_8 (not_8_out, B7);
  Multiplexer #(.select(2), .disabled(0)) multiplexer_1 (
    .in0(B0), .in1(not_1_out), .in2(in_4), .in3(in_5), .out(multiplexer_1_out), .sel(in_34));  // open: en
  Multiplexer #(.select(2), .disabled(0)) multiplexer_2 (
    .in0(B1), .in1(not_2_out), .in2(in_8), .in3(in_9), .out(multiplexer_2_out), .sel(in_34));  // open: en
  Multiplexer #(.select(2), .disabled(0)) multiplexer_3 (
    .in0(B2), .in1(not_3_out), .in2(in_12), .in3(in_13), .out(multiplexer_3_out), .sel(in_34));  // open: en
  Multiplexer #(.select(2), .disabled(0)) multiplexer_4 (
    .in0(B3), .in1(not_4_out), .in2(in_16), .in3(in_17), .out(multiplexer_4_out), .sel(in_34));  // open: en
  Multiplexer #(.select(2), .disabled(0)) multiplexer_5 (
    .in0(B4), .in1(not_5_out), .in2(in_20), .in3(in_21), .out(multiplexer_5_out), .sel(in_34));  // open: en
  Multiplexer #(.select(2), .disabled(0)) multiplexer_6 (
    .in0(B5), .in1(not_6_out), .in2(in_24), .in3(in_25), .out(multiplexer_6_out), .sel(in_34));  // open: en
  Multiplexer #(.select(2), .disabled(0)) multiplexer_7 (
    .in0(B6), .in1(not_7_out), .in2(in_28), .in3(in_29), .out(multiplexer_7_out), .sel(in_34));  // open: en
  Multiplexer #(.select(2), .disabled(0)) multiplexer_8 (
    .in0(B7), .in1(not_8_out), .in2(in_32), .in3(in_33), .out(multiplexer_8_out), .sel(in_34));  // open: en
  Adder #(.width(1)) adder_1 (.a(A0), .b(multiplexer_1_out), .out(D0), .cin(Cin), .cout(adder_1_cout));
  Adder #(.width(1)) adder_2 (.a(A1), .b(multiplexer_2_out), .out(D1), .cin(adder_1_cout), .cout(adder_2_cout));
  Adder #(.width(1)) adder_3 (.a(A2), .b(multiplexer_3_out), .out(D2), .cin(adder_2_cout), .cout(adder_3_cout));
  Adder #(.width(1)) adder_4 (.a(A3), .b(multiplexer_4_out), .out(D3), .cin(adder_3_cout), .cout(adder_4_cout));
  Adder #(.width(1)) adder_5 (.a(A0_2), .b(multiplexer_5_out), .out(D4), .cin(adder_4_cout), .cout(adder_5_cout));
  Adder #(.width(1)) adder_6 (.a(A1_2), .b(multiplexer_6_out), .out(D5), .cin(adder_5_cout), .cout(adder_6_cout));
  Adder #(.width(1)) adder_7 (.a(A2_2), .b(multiplexer_7_out), .out(D6), .cin(adder_6_cout), .cout(adder_7_cout));
  Adder #(.width(1)) adder_8 (.a(A3_2), .b(multiplexer_8_out), .out(D7), .cin(adder_7_cout));  // open: cout
endmodule

module LOGIC_UNIT (
  input  A1,
  input  B1,
  input  A1_2,
  input  B1_2,
  input  A1_3,
  input  B1_3,
  input  A1_4,
  input  A2,
  input  B2,
  input  A2_2,
  input  B2_2,
  input  A2_3,
  input  B2_3,
  input  A2_4,
  input  in_15,
  input  in_16,
  input  in_17,
  input  in_18,
  input  in_19,
  input  in_20,
  input  in_21,
  input  in_22,
  input  in_23,
  input  in_24,
  input  in_25,
  input  in_26,
  input  in_27,
  input  in_28,
  input  in_29,
  input  in_30,
  input  in_31,
  input  in_32,
  input  in_33,
  input  in_34,
  input  in_35,
  input  in_36,
  input  in_37,
  input  in_38,
  input  in_39,
  input  in_40,
  input  in_41,
  input  in_42,
  input  in_43,
  input  in_44,
  input  in_45,
  input  in_46,
  input  in_47,
  input  in_48,
  input  in_49,
  input  in_50,
  input  in_51,
  input  in_52,
  input  in_53,
  input  in_54,
  input  [1:0] in_55,
  input  in_56,
  input  in_57,
  output out_58,
  output out_59,
  output out_60,
  output out_61,
  output out_62,
  output out_63,
  output out_64
);

  wire and_1_out, and_2_out, and_3_out, and_4_out, and_5_out, and_6_out, and_7_out, and_8_out,
       multiplexer_6_out, not_1_out, not_2_out, not_3_out, not_4_out, not_5_out, not_6_out, not_7_out,
       not_8_out, or_1_out, or_2_out, or_3_out, or_4_out, or_5_out, or_6_out, or_7_out, or_8_out, xor_1_out,
       xor_2_out, xor_3_out, xor_4_out, xor_5_out, xor_6_out, xor_7_out, xor_8_out;

  not not_1 (not_1_out, A1_4);
  not not_2 (not_2_out, A2_4);
  not not_3 (not_3_out, in_21);
  not not_4 (not_4_out, in_28);
  not not_5 (not_5_out, in_35);
  not not_6 (not_6_out, in_42);
  not not_7 (not_7_out, in_49);
  not not_8 (not_8_out, in_57);
  and and_1 (and_1_out, A1, B1);
  or or_1 (or_1_out, A1_2, B1_2);
  xor xor_1 (xor_1_out, A1_3, B1_3);
  and and_2 (and_2_out, A2, B2);
  or or_2 (or_2_out, A2_2, B2_2);
  xor xor_2 (xor_2_out, A2_3, B2_3);
  and and_3 (and_3_out, in_15, in_16);
  or or_3 (or_3_out, in_17, in_18);
  xor xor_3 (xor_3_out, in_19, in_20);
  and and_4 (and_4_out, in_22, in_23);
  or or_4 (or_4_out, in_24, in_25);
  xor xor_4 (xor_4_out, in_26, in_27);
  and and_5 (and_5_out, in_29, in_30);
  or or_5 (or_5_out, in_31, in_32);
  xor xor_5 (xor_5_out, in_33, in_34);
  and and_6 (and_6_out, in_36, in_37);
  or or_6 (or_6_out, in_38, in_39);
  xor xor_6 (xor_6_out, in_40, in_41);
  and and_7 (and_7_out, in_43, in_44);
  or or_7 (or_7_out, in_45, in_46);
  xor xor_7 (xor_7_out, in_47, in_48);
  and and_8 (and_8_out, in_50, in_51);
  or or_8 (or_8_out, in_52, in_53);
  xor xor_8 (xor_8_out, in_54, in_56);
  Multiplexer #(.select(2)) multiplexer_1 (
    .in0(and_1_out), .in1(or_1_out), .in2(xor_1_out), .in3(not_1_out), .out(out_58), .sel(in_55));  // open: en
  Multiplexer #(.select(2)) multiplexer_2 (
    .in0(and_2_out), .in1(or_2_out), .in2(xor_2_out), .in3(not_2_out), .out(out_59), .sel(in_55));  // open: en
  Multiplexer #(.select(2)) multiplexer_3 (
    .in0(and_3_out), .in1(or_3_out), .in2(xor_3_out), .in3(not_3_out), .out(out_60), .sel(in_55));  // open: en
  Multiplexer #(.select(2)) multiplexer_4 (
    .in0(and_4_out), .in1(or_4_out), .in2(xor_4_out), .in3(not_4_out), .out(out_61), .sel(in_55));  // open: en
  Multiplexer #(.select(2)) multiplexer_5 (
    .in0(and_5_out), .in1(or_5_out), .in2(xor_5_out), .in3(not_5_out), .out(out_62), .sel(in_55));  // open: en
  Multiplexer #(.select(2)) multiplexer_6 (
    .in0(and_6_out), .in1(or_6_out), .in2(xor_6_out), .in3(not_6_out), .out(multiplexer_6_out), .sel(in_55));  // open: en
  Multiplexer #(.select(2)) multiplexer_7 (
    .in0(and_7_out), .in1(or_7_out), .in2(xor_7_out), .in3(not_7_out), .out(out_63), .sel(in_55));  // open: en
  Multiplexer #(.select(2)) multiplexer_8 (
    .in0(and_8_out), .in1(or_8_out), .in2(xor_8_out), .in3(not_8_out), .out(out_64), .sel(in_55));  // open: en
endmodule
