// Logisim project 8 BIT LOGIC UNIT.circ as structural Verilog: 1 circuit, main circuit main
module main (
  input  A1,
  input  B1,
  input  A1_2,
  input  B1_2,
  input  A1_3,
  input  B1_3,
  input  A1_4,
  input  A2,
  input  B2,
  input  A2_2,
  input  B2_2,
  input  A2_3,
  input  B2_3,
  input  A2_4,
  input  in_15,
  input  in_16,
  input  in_17,
  input  in_18,
  input  in_19,
  input  in_20,
  input  in_21,
  input  in_22,
  input  in_23,
  input  in_24,
  input  in_25,
  input  in_26,
  input  in_27,
  input  in_28,
  input  in_29,
  input  in_30,
  input  in_31,
  input  in_32,
  input  in_33,
  input  in_34,
  input  in_35,
  input  in_36,
  input  in_37,
  input  in_38,
  input  in_39,
  input  in_40,
  input  in_41,
  input  in_42,
  input  in_43,
  input  in_44,
  input  in_45,
  input  in_46,
  input  in_47,
  input  in_48,
  input  in_49,
  input  in_50,
  input  in_51,
  input  in_52,
  input  in_53,
  input  in_54,
  input  [1:0] in_55,
  input  in_56,
  input  in_57,
  output out_58,
  output out_59,
  output out_60,
  output out_61,
  output out_62,
  output out_63,
  output out_64,
  output out_65
);

  wire and_1_out, and_2_out, and_3_out, and_4_out, and_5_out, and_6_out, and_7_out, and_8_out, not_1_out,
       not_2_out, not_3_out, not_4_out, not_5_out, not_6_out, not_7_out, not_8_out, or_1_out, or_2_out,
       or_3_out, or_4_out, or_5_out, or_6_out, or_7_out, or_8_out, xor_1_out, xor_2_out, xor_3_out,
       xor_4_out, xor_5_out, xor_6_out, xor_7_out, xor_8_out;

  not not_1 (not_1_out, A1_4);
  not not_2 (not_2_out, A2_4);
  not not_3 (not_3_out, in_21);
  not not_4 (not_4_out, in_28);
  not not_5 (not_5_out, in_35);
  not not_6 (not_6_out, in_42);
  not not_7 (not_7_out, in_49);
  not not_8 (not_8_out, in_57);
  and and_1 (and_1_out, A1, B1);
  or or_1 (or_1_out, A1_2, B1_2);
  xor xor_1 (xor_1_out, A1_3, B1_3);
  and and_2 (and_2_out, A2, B2);
  or or_2 (or_2_out, A2_2, B2_2);
  xor xor_2 (xor_2_out, A2_3, B2_3);
  and and_3 (and_3_out, in_15, in_16);
  or or_3 (or_3_out, in_17, in_18);
  xor xor_3 (xor_3_out, in_19, in_20);
  and and_4 (and_4_out, in_22, in_23);
  or or_4 (or_4_out, in_24, in_25);
  xor xor_4 (xor_4_out, in_26, in_27);
  and and_5 (and_5_out, in_29, in_30);
  or or_5 (or_5_out, in_31, in_32);
  xor xor_5 (xor_5_out, in_33, in_34);
  and and_6 (and_6_out, in_36, in_37);
  or or_6 (or_6_out, in_38, in_39);
  xor xor_6 (xor_6_out, in_40, in_41);
  and and_7 (and_7_out, in_43, in_44);
  or or_7 (or_7_out, in_45, in_46);
  xor xor_7 (xor_7_out, in_47, in_48);
  and and_8 (and_8_out, in_50, in_51);
  or or_8 (or_8_out, in_52, in_53);
  xor xor_8 (xor_8_out, in_54, in_56);
  Multiplexer #(.select(2)) multiplexer_1 (
    .in0(and_1_out), .in1(or_1_out), .in2(xor_1_out), .in3(not_1_out), .out(out_58), .sel(in_55));  // open: en
  Multiplexer #(.select(2)) multiplexer_2 (
    .in0(and_2_out), .in1(or_2_out), .in2(xor_2_out), .in3(not_2_out), .out(out_59), .sel(in_55));  // open: en
  Multiplexer #(.select(2)) multiplexer_3 (
    .in0(and_3_out), .in1(or_3_out), .in2(xor_3_out), .in3(not_3_out), .out(out_60), .sel(in_55));  // open: en
  Multiplexer #(.select(2)) multiplexer_4 (
    .in0(and_4_out), .in1(or_4_out), .in2(xor_4_out), .in3(not_4_out), .out(out_61), .sel(in_55));  // open: en
  Multiplexer #(.select(2)) multiplexer_5 (
    .in0(and_5_out), .in1(or_5_out), .in2(xor_5_out), .in3(not_5_out), .out(out_62), .sel(in_55));  // open: en
  Multiplexer #(.select(2)) multiplexer_6 (
    .in0(and_6_out), .in1(or_6_out), .in2(xor_6_out), .in3(not_6_out), .out(out_63), .sel(in_55));  // open: en
  Multiplexer #(.select(2)) multiplexer_7 (
    .in0(and_7_out), .in1(or_7_out), .in2(xor_7_out), .in3(not_7_out), .out(out_64), .sel(in_55));  // open: en
  Multiplexer #(.select(2)) multiplexer_8 (
    .in0(and_8_out), .in1(or_8_out), .in2(xor_8_out), .in3(not_8_out), .out(out_65), .sel(in_55));  // open: en
endmodule
