// Logisim project AC LOAD MAIN.circ as structural Verilog: 1 circuit, main circuit main
module main (
  input  t5,
  input  D0,
  input  D1,
  input  D2,
  input  D6,
  input  T3,
  input  D7,
  input  I,
  input  IR_5,
  input  IR_6,
  input  IR_7,
  input  IR_9,
  input  ir_11,
  output AND,
  output ADD,
  output DR,
  output SUB,
  output clr,
  output INC,
  output SHL,
  output SHR,
  output COM,
  output INPR
);

  wire and_1_out, not_1_out;

  not not_1 (not_1_out, I);
  and and_1 (and_1_out, T3, D7);
  and lda (DR, t5, D2);
  and and_2 (AND, t5, D0);
  and u_add (ADD, D1, t5);
  and u_SUB (SUB, D6, t5);
  and CLA (clr, not_1_out, and_1_out, ir_11);
  and u_INC (INC, and_1_out, not_1_out, IR_5);
  and u_SHL (SHL, not_1_out, and_1_out, IR_6);
  and u_SHR (SHR, not_1_out, and_1_out, IR_7);
  and u_COM (COM, not_1_out, and_1_out, IR_9);
  and u_INPR (INPR, and_1_out, I, ir_11);
endmodule
