// Logisim project ALU_16_BIT.circ as structural Verilog: 1 circuit, main circuit main
module main (
  input  [15:0] DR_16_BIT,
  input  [15:0] AC__16_BIT,
  input  CLK,
  input  LOAD,
  input  T5,
  input  D0,
  input  D1,
  input  D2,
  input  D6,
  input  T3,
  input  D7,
  input  I,
  input  IR5,
  input  IR6,
  input  IR7,
  input  IR9,
  input  IR11,
  input  [7:0] INPR__8_BIT,
  output [15:0] AC__OUT_16
);

  wire clock_1_out, main_1_c_out, main_1_c_out_add, main_1_c_out_sub, main_2_c_out_add, main_3_c_out,
       main_3_c_out_add, main_3_c_out_sub, main_4_c_out, main_4_c_out_add, main_4_c_out_sub, main_5_c_out,
       main_5_c_out_add, main_5_c_out_sub, main_6_c_out, main_6_c_out_add, main_6_c_out_sub, main_7_c_out,
       main_7_c_out_add, main_7_c_out_sub, main_8_c_out, main_8_c_out_add, main_8_c_out_sub, main_9_c_out,
       main_9_c_out_add, main_9_c_out_sub, main_10_c_out, main_10_c_out_add, main_10_c_out_sub,
       main_11_c_out, main_11_c_out_add, main_11_c_out_sub, main_12_c_out, main_12_c_out_add,
       main_12_c_out_sub, main_13_c_out, main_13_c_out_add, main_13_c_out_sub, main_14_c_out,
       main_14_c_out_add, main_14_c_out_sub, main_15_c_out, main_15_c_out_add, main_15_c_out_sub,
       main_16_c_out, main_16_c_out_add, main_16_c_out_sub;

  Clock clock_1 (.out(clock_1_out));
  _1_bit_ALU_main main_1 (
    .T5(T5), .D0(D0), .D1(D1), .D2(D2), .D6(D6), .T3(T3), .D7(D7), .I(I), .IR_5(IR5), .IR_6(IR6), .IR_7(IR7),
    .IR_9(IR9), .IR_11(IR11), .INPR___i__th_BIT(INPR__8_BIT[7]), .AC_i_1(AC__16_BIT[6]),
    .AC_i_1_2(AC__16_BIT[8]), .DR_i(DR_16_BIT[7]), .AC__i(AC__16_BIT[7]), .c_in__add(main_4_c_out_add),
    .c_in__sub(main_4_c_out_sub), .C_IN_INC(main_4_c_out), .LOAD(LOAD), .CLK(clock_1_out),
    .AC__i_2(AC__OUT_16[7]), .c_out(main_1_c_out), .c_out_sub(main_1_c_out_sub), .c_out_add(main_1_c_out_add));
  _1_bit_ALU_main main_2 (
    .T5(T5), .D0(D0), .D1(D1), .D2(D2), .D6(D6), .T3(T3), .D7(D7), .I(I), .IR_5(IR5), .IR_6(IR6), .IR_7(IR7),
    .IR_9(IR9), .IR_11(IR11), .INPR___i__th_BIT(1'b0), .AC_i_1(AC__16_BIT[14]), .AC_i_1_2(main_2_c_out_add),
    .DR_i(DR_16_BIT[15]), .AC__i(AC__16_BIT[15]), .c_in__add(main_3_c_out_add), .c_in__sub(main_3_c_out_sub),
    .C_IN_INC(main_3_c_out), .LOAD(LOAD), .CLK(clock_1_out), .AC__i_2(AC__OUT_16[15]),
    .c_out_add(main_2_c_out_add));  // open: c_out, c_out_sub
  _1_bit_ALU_main main_3 (
    .T5(T5), .D0(D0), .D1(D1), .D2(D2), .D6(D6), .T3(T3), .D7(D7), .I(I), .IR_5(IR5), .IR_6(IR6), .IR_7(IR7),
    .IR_9(IR9), .IR_11(IR11), .INPR___i__th_BIT(1'b0), .AC_i_1(AC__16_BIT[13]), .AC_i_1_2(AC__16_BIT[15]),
    .DR_i(DR_16_BIT[14]), .AC__i(AC__16_BIT[14]), .c_in__add(main_5_c_out_add), .c_in__sub(main_5_c_out_sub),
    .C_IN_INC(main_5_c_out), .LOAD(LOAD), .CLK(clock_1_out), .AC__i_2(AC__OUT_16[14]), .c_out(main_3_c_out),
    .c_out_sub(main_3_c_out_sub), .c_out_add(main_3_c_out_add));
  _1_bit_ALU_main main_4 (
    .T5(T5), .D0(D0), .D1(D1), .D2(D2), .D6(D6), .T3(T3), .D7(D7), .I(I), .IR_5(IR5), .IR_6(IR6), .IR_7(IR7),
    .IR_9(IR9), .IR_11(IR11), .INPR___i__th_BIT(INPR__8_BIT[6]), .AC_i_1(AC__16_BIT[5]),
    .AC_i_1_2(AC__16_BIT[7]), .DR_i(DR_16_BIT[6]), .AC__i(AC__16_BIT[6]), .c_in__add(main_6_c_out_add),
    .c_in__sub(main_6_c_out_sub), .C_IN_INC(main_6_c_out), .LOAD(LOAD), .CLK(clock_1_out),
    .AC__i_2(AC__OUT_16[6]), .c_out(main_4_c_out), .c_out_sub(main_4_c_out_sub), .c_out_add(main_4_c_out_add));
  _1_bit_ALU_main main_5 (
    .T5(T5), .D0(D0), .D1(D1), .D2(D2), .D6(D6), .T3(T3), .D7(D7), .I(I), .IR_5(IR5), .IR_6(IR6), .IR_7(IR7),
    .IR_9(IR9), .IR_11(IR11), .INPR___i__th_BIT(1'b0), .AC_i_1(AC__16_BIT[12]), .AC_i_1_2(AC__16_BIT[14]),
    .DR_i(DR_16_BIT[13]), .AC__i(AC__16_BIT[13]), .c_in__add(main_7_c_out_add), .c_in__sub(main_7_c_out_sub),
    .C_IN_INC(main_7_c_out), .LOAD(LOAD), .CLK(clock_1_out), .AC__i_2(AC__OUT_16[13]), .c_out(main_5_c_out),
    .c_out_sub(main_5_c_out_sub), .c_out_add(main_5_c_out_add));
  _1_bit_ALU_main main_6 (
    .T5(T5), .D0(D0), .D1(D1), .D2(D2), .D6(D6), .T3(T3), .D7(D7), .I(I), .IR_5(IR5), .IR_6(IR6), .IR_7(IR7),
    .IR_9(IR9), .IR_11(IR11), .INPR___i__th_BIT(INPR__8_BIT[5]), .AC_i_1(AC__16_BIT[4]),
    .AC_i_1_2(AC__16_BIT[6]), .DR_i(DR_16_BIT[5]), .AC__i(AC__16_BIT[5]), .c_in__add(main_8_c_out_add),
    .c_in__sub(main_8_c_out_sub), .C_IN_INC(main_8_c_out), .LOAD(LOAD), .CLK(clock_1_out),
    .AC__i_2(AC__OUT_16[5]), .c_out(main_6_c_out), .c_out_sub(main_6_c_out_sub), .c_out_add(main_6_c_out_add));
  _1_bit_ALU_main main_7 (
    .T5(T5), .D0(D0), .D1(D1), .D2(D2), .D6(D6), .T3(T3), .D7(D7), .I(I), .IR_5(IR5), .IR_6(IR6), .IR_7(IR7),
    .IR_9(IR9), .IR_11(IR11), .INPR___i__th_BIT(1'b0), .AC_i_1(AC__16_BIT[11]), .AC_i_1_2(AC__16_BIT[13]),
    .DR_i(DR_16_BIT[12]), .AC__i(AC__16_BIT[12]), .c_in__add(main_9_c_out_add), .c_in__sub(main_9_c_out_sub),
    .C_IN_INC(main_9_c_out), .LOAD(LOAD), .CLK(clock_1_out), .AC__i_2(AC__OUT_16[12]), .c_out(main_7_c_out),
    .c_out_sub(main_7_c_out_sub), .c_out_add(main_7_c_out_add));
  _1_bit_ALU_main main_8 (
    .T5(T5), .D0(D0), .D1(D1), .D2(D2), .D6(D6), .T3(T3), .D7(D7), .I(I), .IR_5(IR5), .IR_6(IR6), .IR_7(IR7),
    .IR_9(IR9), .IR_11(IR11), .INPR___i__th_BIT(INPR__8_BIT[4]), .AC_i_1(AC__16_BIT[3]),
    .AC_i_1_2(AC__16_BIT[5]), .DR_i(DR_16_BIT[4]), .AC__i(AC__16_BIT[4]), .c_in__add(main_10_c_out_add),
    .c_in__sub(main_10_c_out_sub), .C_IN_INC(main_10_c_out), .LOAD(LOAD), .CLK(clock_1_out),
    .AC__i_2(AC__OUT_16[4]), .c_out(main_8_c_out), .c_out_sub(main_8_c_out_sub), .c_out_add(main_8_c_out_add));
  _1_bit_ALU_main main_9 (
    .T5(T5), .D0(D0), .D1(D1), .D2(D2), .D6(D6), .T3(T3), .D7(D7), .I(I), .IR_5(IR5), .IR_6(IR6), .IR_7(IR7),
    .IR_9(IR9), .IR_11(IR11), .INPR___i__th_BIT(1'b0), .AC_i_1(AC__16_BIT[10]), .AC_i_1_2(AC__16_BIT[12]),
    .DR_i(DR_16_BIT[11]), .AC__i(AC__16_BIT[11]), .c_in__add(main_11_c_out_add),
    .c_in__sub(main_11_c_out_sub), .C_IN_INC(main_11_c_out), .LOAD(LOAD), .CLK(clock_1_out),
    .AC__i_2(AC__OUT_16[11]), .c_out(main_9_c_out), .c_out_sub(main_9_c_out_sub), .c_out_add(main_9_c_out_add));
  _1_bit_ALU_main main_10 (
    .T5(T5), .D0(D0), .D1(D1), .D2(D2), .D6(D6), .T3(T3), .D7(D7), .I(I), .IR_5(IR5), .IR_6(IR6), .IR_7(IR7),
    .IR_9(IR9), .IR_11(IR11), .INPR___i__th_BIT(INPR__8_BIT[3]), .AC_i_1(AC__16_BIT[2]),
    .AC_i_1_2(AC__16_BIT[4]), .DR_i(DR_16_BIT[3]), .AC__i(AC__16_BIT[3]), .c_in__add(main_12_c_out_add),
    .c_in__sub(main_12_c_out_sub), .C_IN_INC(main_12_c_out), .LOAD(LOAD), .CLK(clock_1_out),
    .AC__i_2(AC__OUT_16[3]), .c_out(main_10_c_out), .c_out_sub(main_10_c_out_sub),
    .c_out_add(main_10_c_out_add));
  _1_bit_ALU_main main_11 (
    .T5(T5), .D0(D0), .D1(D1), .D2(D2), .D6(D6), .T3(T3), .D7(D7), .I(I), .IR_5(IR5), .IR_6(IR6), .IR_7(IR7),
    .IR_9(IR9), .IR_11(IR11), .INPR___i__th_BIT(1'b0), .AC_i_1(AC__16_BIT[9]), .AC_i_1_2(AC__16_BIT[11]),
    .DR_i(DR_16_BIT[10]), .AC__i(AC__16_BIT[10]), .c_in__add(main_13_c_out_add),
    .c_in__sub(main_13_c_out_sub), .C_IN_INC(main_13_c_out), .LOAD(LOAD), .CLK(clock_1_out),
    .AC__i_2(AC__OUT_16[10]), .c_out(main_11_c_out), .c_out_sub(main_11_c_out_sub),
    .c_out_add(main_11_c_out_add));
  _1_bit_ALU_main main_12 (
    .T5(T5), .D0(D0), .D1(D1), .D2(D2), .D6(D6), .T3(T3), .D7(D7), .I(I), .IR_5(IR5), .IR_6(IR6), .IR_7(IR7),
    .IR_9(IR9), .IR_11(IR11), .INPR___i__th_BIT(INPR__8_BIT[2]), .AC_i_1(AC__16_BIT[1]),
    .AC_i_1_2(AC__16_BIT[3]), .DR_i(DR_16_BIT[2]), .AC__i(AC__16_BIT[2]), .c_in__add(main_14_c_out_add),
    .c_in__sub(main_14_c_out_sub), .C_IN_INC(main_14_c_out), .LOAD(LOAD), .CLK(clock_1_out),
    .AC__i_2(AC__OUT_16[2]), .c_out(main_12_c_out), .c_out_sub(main_12_c_out_sub),
    .c_out_add(main_12_c_out_add));
  _1_bit_ALU_main main_13 (
    .T5(T5), .D0(D0), .D1(D1), .D2(D2), .D6(D6), .T3(T3), .D7(D7), .I(I), .IR_5(IR5), .IR_6(IR6), .IR_7(IR7),
    .IR_9(IR9), .IR_11(IR11), .INPR___i__th_BIT(1'b0), .AC_i_1(AC__16_BIT[8]), .AC_i_1_2(AC__16_BIT[10]),
    .DR_i(DR_16_BIT[9]), .AC__i(AC__16_BIT[9]), .c_in__add(main_15_c_out_add), .c_in__sub(main_15_c_out_sub),
    .C_IN_INC(main_15_c_out), .LOAD(LOAD), .CLK(clock_1_out), .AC__i_2(AC__OUT_16[9]), .c_out(main_13_c_out),
    .c_out_sub(main_13_c_out_sub), .c_out_add(main_13_c_out_add));
  _1_bit_ALU_main main_14 (
    .T5(T5), .D0(D0), .D1(D1), .D2(D2), .D6(D6), .T3(T3), .D7(D7), .I(I), .IR_5(IR5), .IR_6(IR6), .IR_7(IR7),
    .IR_9(IR9), .IR_11(IR11), .INPR___i__th_BIT(INPR__8_BIT[1]), .AC_i_1(AC__16_BIT[0]),
    .AC_i_1_2(AC__16_BIT[2]), .DR_i(DR_16_BIT[1]), .AC__i(AC__16_BIT[1]), .c_in__add(main_16_c_out_add),
    .c_in__sub(main_16_c_out_sub), .C_IN_INC(main_16_c_out), .LOAD(LOAD), .CLK(clock_1_out),
    .AC__i_2(AC__OUT_16[1]), .c_out(main_14_c_out), .c_out_sub(main_14_c_out_sub),
    .c_out_add(main_14_c_out_add));
  _1_bit_ALU_main main_15 (
    .T5(T5), .D0(D0), .D1(D1), .D2(D2), .D6(D6), .T3(T3), .D7(D7), .I(I), .IR_5(IR5), .IR_6(IR6), .IR_7(IR7),
    .IR_9(IR9), .IR_11(IR11), .INPR___i__th_BIT(1'b0), .AC_i_1(AC__16_BIT[7]), .AC_i_1_2(AC__16_BIT[9]),
    .DR_i(DR_16_BIT[8]), .AC__i(AC__16_BIT[8]), .c_in__add(main_1_c_out_add), .c_in__sub(main_1_c_out_sub),
    .C_IN_INC(main_1_c_out), .LOAD(LOAD), .CLK(clock_1_out), .AC__i_2(AC__OUT_16[8]), .c_out(main_15_c_out),
    .c_out_sub(main_15_c_out_sub), .c_out_add(main_15_c_out_add));
  _2nd_1_bit_ALU_main main_16 (
    .T5(T5), .D0(D0), .D1(D1), .D2(D2), .D6(D6), .T3(T3), .D7(D7), .I(I), .IR_5(IR5), .IR_6(IR6), .IR_7(IR7),
    .IR_9(IR9), .IR_11(IR11), .INPR___i__th_BIT(INPR__8_BIT[0]), .AC_i_1(main_2_c_out_add),
    .AC_i_1_2(AC__16_BIT[1]), .DR_i(DR_16_BIT[0]), .AC__i(AC__16_BIT[0]), .LOAD(LOAD), .CLK(clock_1_out),
    .AC__i_2(AC__OUT_16[0]), .c_out(main_16_c_out), .c_out_sub(main_16_c_out_sub),
    .c_out_add(main_16_c_out_add));  // open: c_in__add, c_in__sub, C_IN_INC
endmodule
