// Logisim project AR Complete.circ as structural Verilog: 1 circuit, main circuit main
module main (
  input  in_1,
  input  [11:0] AR_IN,
  input  r,
  input  t0,
  input  t2,
  input  t3,
  input  t4,
  input  I,
  input  d5,
  input  d7_prime,
  output [11:0] AR_OUT
);

  wire clock_1_out, main_1_p9, main_1_p10, main_1_p11;

  // ar_load_main_main main_1: pin names not known; wires that end beside it: r, t0, t2, t3, t4, I, d5, d7_prime, main_1_p9, main_1_p10, main_1_p11
  Clock clock_1 (.out(clock_1_out));
  // _12_bit_res_main main_2: pin names not known; wires that end beside it: in_1, clock_1_out, AR_IN[0], AR_IN[1], AR_IN[2], AR_IN[3], AR_IN[4], AR_IN[5], main_1_p9, main_1_p11, main_1_p10, AR_IN[6], AR_IN[7], AR_IN[8], AR_IN[9], AR_IN[10], AR_IN[11], AR_OUT[0], AR_OUT[1], AR_OUT[2], AR_OUT[3], AR_OUT[4], AR_OUT[5], AR_OUT[6], AR_OUT[7], AR_OUT[8], AR_OUT[9], AR_OUT[10], AR_OUT[11]
endmodule
