// Logisim project MAIN CIRCUIT.circ as structural Verilog: 1 circuit, main circuit main
module main (
  output O,
  output U
);

  wire AR_p4, AR_p5, F1_F2_F3_p13, F1_F2_F3_p14, F1_F2_F3_p15, or_1_out, or_2_out, Sequencer_p1,
       Sequencer_p3, Sequencer_p5;
  wire [1:0] F1_F2_F3_p8, F1_F2_F3_p20, priority_encoder_1_p3, undriven;
  wire [2:0] Sequencer_p8_2;
  wire [3:0] PC_p3, PC_p3_2, Sequencer_p8;
  wire [4:0] Sequencer_p4_2;
  wire [6:0] Sequencer_p7;
  wire [10:0] AR_p7, F1_F2_F3_p4, multiplexer_1_out, Sequencer_p4;
  wire [10:8] PC_p3_3;
  wire [15:0] multiplexer_2_out, RAM_p6, Sequencer_p2;

  Multiplexer #(.width(11)) multiplexer_1 (
    .in0({PC_p3_3, PC_p3_2, PC_p3}), .in1(Sequencer_p4), .out(multiplexer_1_out), .sel(undriven[0]),
    .en(AR_p4));
  or or_1 (or_1_out, undriven[1], undriven[0]);
  // _11BitRegister_main AR: pin names not known; wires that end beside it: 1'b0, or_1_out, 1'b0, AR_p4, AR_p5, multiplexer_1_out, AR_p7
  // _11BitRegister_main PC: pin names not known; wires that end beside it: AR_p5, AR_p7, {PC_p3_3, PC_p3_2, PC_p3}
  // main_main Sequencer: pin names not known; wires that end beside it: Sequencer_p1, Sequencer_p2, Sequencer_p3, {Sequencer_p4_2, Sequencer_p4}, Sequencer_p5, AR_p5, Sequencer_p7, {Sequencer_p8_2, Sequencer_p8}
  // DecodeMicropLogic_main F1_F2_F3: pin names not known; wires that end beside it: Sequencer_p1, Sequencer_p3, Sequencer_p5, F1_F2_F3_p4[0], F1_F2_F3_p4[1], F1_F2_F3_p4[2], F1_F2_F3_p4[3], F1_F2_F3_p8[0], F1_F2_F3_p4[4], F1_F2_F3_p4[5], F1_F2_F3_p4[6], F1_F2_F3_p8[1], F1_F2_F3_p13, F1_F2_F3_p14, F1_F2_F3_p15, F1_F2_F3_p4[7], F1_F2_F3_p4[8], F1_F2_F3_p4[9], F1_F2_F3_p4[10], F1_F2_F3_p20[0], F1_F2_F3_p20[1]
  // Priority_Encoder #(.select(2)) priority_encoder_1: pin names not known; wires that end beside it: F1_F2_F3_p15, F1_F2_F3_p8[1], priority_encoder_1_p3, F1_F2_F3_p13, 1'b0
  or or_2 (or_2_out, F1_F2_F3_p15, F1_F2_F3_p8[1], F1_F2_F3_p13);
  // Ram2048X16_main RAM: pin names not known; wires that end beside it: F1_F2_F3_p8[0], F1_F2_F3_p8[1], {Sequencer_p4_2, Sequencer_p4}, AR_p5, AR_p7, RAM_p6
  Multiplexer #(.select(2), .width(16)) multiplexer_2 (
    .in0({{5{1'b0}}, PC_p3_3, PC_p3_2, PC_p3}), .in1(RAM_p6), .in2(Sequencer_p2), .out(multiplexer_2_out),
    .sel(priority_encoder_1_p3));  // open: in3, en
  // _16BitRegister_main DR: pin names not known; wires that end beside it: F1_F2_F3_p14, or_2_out, AR_p5, multiplexer_2_out, {Sequencer_p4_2, Sequencer_p4}
  Clock Clock (.out(AR_p5));
  // ALU_main main_1: pin names not known; wires that end beside it: F1_F2_F3_p4, AR_p5, {Sequencer_p4_2, Sequencer_p4}, Sequencer_p2, O, U
  Hex_Digit_Display hex_digit_display_1 (.value(Sequencer_p2[15:12]));  // open: dp
  Hex_Digit_Display hex_digit_display_2 (.value(Sequencer_p2[11:8]));  // open: dp
  Hex_Digit_Display hex_digit_display_3 (.value(Sequencer_p2[15:12]));  // open: dp
  Hex_Digit_Display hex_digit_display_4 (.value(Sequencer_p2[11:8]));  // open: dp
  Hex_Digit_Display hex_digit_display_5 (.value({AR_p7[10:8], 1'b0}));  // open: dp
  Hex_Digit_Display hex_digit_display_6 (.value(AR_p7[7:4]));  // open: dp
  Hex_Digit_Display hex_digit_display_7 (.value(Sequencer_p2[7:4]));  // open: dp
  Hex_Digit_Display hex_digit_display_8 (.value(Sequencer_p2[3:0]));  // open: dp
  Hex_Digit_Display hex_digit_display_9 (.value(Sequencer_p2[7:4]));  // open: dp
  Hex_Digit_Display hex_digit_display_10 (.value(Sequencer_p2[3:0]));  // open: dp
  Hex_Digit_Display hex_digit_display_11 (.value(AR_p7[3:0]));  // open: dp
  Hex_Digit_Display hex_digit_display_12 (.value({PC_p3_3, 1'b0}));  // open: dp
  Hex_Digit_Display hex_digit_display_13 (.value({1'b0, Sequencer_p7[6:4]}));  // open: dp
  Hex_Digit_Display hex_digit_display_14 (.value(Sequencer_p7[3:0]));  // open: dp
  Hex_Digit_Display hex_digit_display_15 (.value(PC_p3_2));  // open: dp
  Hex_Digit_Display hex_digit_display_16 (.value({1'b0, Sequencer_p8_2}));  // open: dp
  Hex_Digit_Display hex_digit_display_17 (.value(PC_p3));  // open: dp
  Hex_Digit_Display hex_digit_display_18 (.value(Sequencer_p8));  // open: dp

  // Notes on the sheet:
  //   Computer 2
  //   AR
  //   DR
  //   AC
  //   SBR
  //   PC
  //   CAR
endmodule
